// Logisim project Processor.circ as structural Verilog: 6 circuits, main circuit main
module main (
);

  wire adder_3_cout, button_1_out, CLK, clock_1_out, clock_2_out, controlunit_1_alusrc, controlunit_1_immsrc,
       controlunit_1_memtoreg, controlunit_1_memwrite, controlunit_1_pcsrc, controlunit_1_regwrite,
       not_1_out, xnor_1_out, xor_1_out, xor_2_out;
  wire [1:0] controlunit_1_alucontrol, controlunit_1_regsrc;
  wire [3:0] aluw_flags_1_aluflags, aluw_flags_2_aluflags, multiplexer_2_out, multiplexer_3_out, rom_1_data_2;
  wire [23:0] adder_1_out, adder_2_out, multiplexer_1_out, multiplexer_5_out, PC_q;
  wire [31:0] adder_3_out, ALU_result, aluw_flags_1_result, aluw_flags_2_result, bit_extender_1_out,
       multiplexer_4_out, ram_1_data, REG_rd1, REG_rd2, registerfield_1_rd1, rom_1_data, undriven;
  wire [31:24] multiplexer_5_out_2;

  NotExactlyOne xnor_1 (.out(xnor_1_out), .in0(1'b1), .in1(1'b1), .in2(1'b0));
  Multiplexer #(.width(24), .enable("false")) multiplexer_1 (
    .in0(multiplexer_5_out), .in1(adder_1_out), .out(multiplexer_1_out), .sel(controlunit_1_pcsrc));
  xor xor_1 (xor_1_out, 1'b1, 1'b1);
  Register #(.width(24)) PC (.D(multiplexer_1_out), .Q(PC_q), .clk(CLK));  // open: en, clr
  xor xor_2 (xor_2_out, xor_1_out, 1'b0);
  Adder #(.width(24)) adder_1 (.a(PC_q), .b(24'h1), .out(adder_1_out));  // open: cin, cout
  Clock u_CLK (.out(CLK));
  not not_1 (not_1_out, xor_2_out);
  ROM #(.addrWidth(24), .dataWidth(32)) rom_1 (
    .addr(PC_q), .data({rom_1_data[31:16], rom_1_data_2, rom_1_data[11:0]}));  // open: sel
  Adder #(.width(24)) adder_2 (.a(adder_1_out), .b(24'h1), .out(adder_2_out));  // open: cin, cout
  assign bit_extender_1_out = {{8{1'b0}}, adder_2_out};  // Bit_Extender bit_extender_1
  Button button_1 (.out(button_1_out));
  ControlUnit controlunit_1 (
    .Cond(rom_1_data[31:28]), .Opt(rom_1_data[27:26]), .Funct(rom_1_data[25:20]), .Rd(rom_1_data_2),
    .PCSrc(controlunit_1_pcsrc), .MemtoReg(controlunit_1_memtoreg), .MemWrite(controlunit_1_memwrite),
    .ALUControl(controlunit_1_alucontrol), .ALUSrc(controlunit_1_alusrc), .ImmSrc(controlunit_1_immsrc),
    .RegWrite(controlunit_1_regwrite), .RegSrc(controlunit_1_regsrc), .Flags(aluw_flags_1_aluflags));
  RegisterField registerfield_1 (
    .A1(4'b0000), .A2(4'b0000), .A3(4'b0000), .WE3(button_1_out), .WD3(32'h2a), .RD1(registerfield_1_rd1),
    .CLK(clock_1_out));  // open: RD2, R15
  Multiplexer #(.width(4), .enable("false")) multiplexer_2 (
    .in0(rom_1_data[19:16]), .in1(4'b1111), .out(multiplexer_2_out), .sel(controlunit_1_regsrc[0]));
  ALU ALU (.B(32'h3), .A(32'h16), .Result(ALU_result), .ALUControl(2'b01));  // open: ALUFlags
  Multiplexer #(.width(4), .enable("false")) multiplexer_3 (
    .in0(rom_1_data[3:0]), .in1(rom_1_data_2), .out(multiplexer_3_out), .sel(controlunit_1_regsrc[1]));
  Register #(.width(32)) register_1 (.D(registerfield_1_rd1), .clk(clock_1_out));  // open: en, Q, clr
  RegisterField REG (
    .A1(multiplexer_2_out), .A2(multiplexer_3_out), .A3(rom_1_data_2), .WE3(controlunit_1_regwrite),
    .WD3({multiplexer_5_out_2, multiplexer_5_out}), .RD1(REG_rd1), .RD2(REG_rd2), .CLK(CLK),
    .R15(bit_extender_1_out));
  Register #(.width(32)) register_2 (.D(ALU_result), .clk(clock_1_out));  // open: en, Q, clr
  Clock clock_1 (.out(clock_1_out));
  Extender extender_1 (
    .In({rom_1_data[23:16], rom_1_data_2, rom_1_data[11:0]}), .Out(undriven), .ImmSrc(controlunit_1_immsrc));
  Multiplexer #(.width(32), .enable("false")) multiplexer_4 (
    .in0(REG_rd2), .in1(undriven), .out(multiplexer_4_out), .sel(controlunit_1_alusrc));
  ALUw_Flags aluw_flags_1 (
    .B(multiplexer_4_out), .A(REG_rd1), .Result(aluw_flags_1_result), .ALUFlags(aluw_flags_1_aluflags),
    .ALUControl(controlunit_1_alucontrol));
  Adder #(.width(32)) adder_3 (.a(32'h6), .b(32'h6), .out(adder_3_out), .cout(adder_3_cout));  // open: cin
  LED led_1 (.in(adder_3_cout));
  ALUw_Flags aluw_flags_2 (
    .B(32'h6), .A(32'h6), .Result(aluw_flags_2_result), .ALUFlags(aluw_flags_2_aluflags), .ALUControl(2'b01));
  Clock clock_2 (.out(clock_2_out));
  RAM #(.addrWidth(24), .dataWidth(32), .bus("separate")) ram_1 (
    .addr(aluw_flags_1_result[23:0]), .din(REG_rd2), .data(ram_1_data), .str(controlunit_1_memwrite),
    .clk(CLK));  // open: sel, ld, clr
  LED led_2 (.in(aluw_flags_2_aluflags[0]));
  LED led_3 (.in(aluw_flags_2_aluflags[1]));
  LED led_4 (.in(aluw_flags_2_aluflags[2]));
  LED led_5 (.in(aluw_flags_2_aluflags[3]));
  Register #(.width(32)) register_3 (.D(aluw_flags_2_result), .clk(clock_2_out));  // open: en, Q, clr
  Multiplexer #(.width(32), .enable("false")) multiplexer_5 (
    .in0(aluw_flags_1_result), .in1(ram_1_data), .out({multiplexer_5_out_2, multiplexer_5_out}),
    .sel(controlunit_1_memtoreg));

  // Notes on the sheet:
  //   PCPlus1
  //   contents of rom_1 (hex, n*v repeats v):
  //   0 2 3 4 5 6 7 8 9 a b c d e f 10
  //   PCPlus2
  //   00: ADD, 01: SUB, 10 AND, 11 OR
  //   Overflow
  //   Carry
  //   Zero
  //   Negative
endmodule

module ALU (
  input  [1:0] ALUControl,
  input  [31:0] B,
  input  [31:0] A,
  output [3:0] ALUFlags,
  output [31:0] Result
);

  wire [31:0] adder_1_out, and_1_out, multiplexer_1_out, not_1_out, or_1_out;

  Multiplexer #(.width(32), .enable("false")) multiplexer_1 (
    .in0(B), .in1(not_1_out), .out(multiplexer_1_out), .sel(ALUControl[0]));
  assign not_1_out = ~B;  // NOT_Gate not_1, 32 bits wide
  Adder #(.width(32)) adder_1 (.a(multiplexer_1_out), .b(A), .out(adder_1_out), .cin(ALUControl[0]));  // open: cout
  assign and_1_out = B & A;  // AND_Gate and_1, 32 bits wide
  assign or_1_out = B | A;  // OR_Gate or_1, 32 bits wide
  Multiplexer #(.select(2), .width(32), .enable("false")) multiplexer_2 (
    .in0(adder_1_out), .in1(adder_1_out), .in2(and_1_out), .in3(or_1_out), .out(Result), .sel(ALUControl));
endmodule

module RegisterField (
  input  CLK,
  input  [3:0] A1,
  input  [3:0] A2,
  input  [3:0] A3,
  input  WE3,
  input  [31:0] WD3,
  input  [31:0] R15,
  output [31:0] RD1,
  output [31:0] RD2
);

  wire demultiplexer_1_out0, demultiplexer_1_out1, demultiplexer_1_out2, demultiplexer_1_out3,
       demultiplexer_1_out4, demultiplexer_1_out5, demultiplexer_1_out6, demultiplexer_1_out7,
       demultiplexer_1_out8, demultiplexer_1_out9, demultiplexer_1_out10, demultiplexer_1_out11,
       demultiplexer_1_out12, demultiplexer_1_out13, demultiplexer_1_out14, demultiplexer_1_out15;
  wire [31:0] r0_q, r1_q, r2_q, r3_q, r4_q, r5_q, r6_q, r7_q, r8_q, r9_q, r10_q, r11_q, r12_q, r13_q, r14_q,
       r15_q;

  Demultiplexer #(.select(4), .enable("false")) demultiplexer_1 (
    .out0(demultiplexer_1_out0), .out1(demultiplexer_1_out1), .out2(demultiplexer_1_out2),
    .out3(demultiplexer_1_out3), .out4(demultiplexer_1_out4), .out5(demultiplexer_1_out5),
    .out6(demultiplexer_1_out6), .out7(demultiplexer_1_out7), .out8(demultiplexer_1_out8),
    .out9(demultiplexer_1_out9), .out10(demultiplexer_1_out10), .out11(demultiplexer_1_out11),
    .out12(demultiplexer_1_out12), .out13(demultiplexer_1_out13), .out14(demultiplexer_1_out14),
    .out15(demultiplexer_1_out15), .in(WE3), .sel(A3));
  Register #(.width(32)) r0 (.D(WD3), .en(demultiplexer_1_out0), .Q(r0_q), .clk(CLK));  // open: clr
  Register #(.width(32)) r4 (.D(WD3), .en(demultiplexer_1_out4), .Q(r4_q), .clk(CLK));  // open: clr
  Register #(.width(32)) r8 (.D(WD3), .en(demultiplexer_1_out8), .Q(r8_q), .clk(CLK));  // open: clr
  Register #(.width(32)) r12 (.D(WD3), .en(demultiplexer_1_out12), .Q(r12_q), .clk(CLK));  // open: clr
  Register #(.width(32)) r1 (.D(WD3), .en(demultiplexer_1_out1), .Q(r1_q), .clk(CLK));  // open: clr
  Register #(.width(32)) r5 (.D(WD3), .en(demultiplexer_1_out5), .Q(r5_q), .clk(CLK));  // open: clr
  Register #(.width(32)) r9 (.D(WD3), .en(demultiplexer_1_out9), .Q(r9_q), .clk(CLK));  // open: clr
  Register #(.width(32)) r13 (.D(WD3), .en(demultiplexer_1_out13), .Q(r13_q), .clk(CLK));  // open: clr
  Register #(.width(32)) r2 (.D(WD3), .en(demultiplexer_1_out2), .Q(r2_q), .clk(CLK));  // open: clr
  Register #(.width(32)) r6 (.D(WD3), .en(demultiplexer_1_out6), .Q(r6_q), .clk(CLK));  // open: clr
  Register #(.width(32)) r10 (.D(WD3), .en(demultiplexer_1_out10), .Q(r10_q), .clk(CLK));  // open: clr
  Register #(.width(32)) r14 (.D(WD3), .en(demultiplexer_1_out14), .Q(r14_q), .clk(CLK));  // open: clr
  Register #(.width(32)) r3 (.D(WD3), .en(demultiplexer_1_out3), .Q(r3_q), .clk(CLK));  // open: clr
  Register #(.width(32)) r7 (.D(WD3), .en(demultiplexer_1_out7), .Q(r7_q), .clk(CLK));  // open: clr
  Register #(.width(32)) r11 (.D(WD3), .en(demultiplexer_1_out11), .Q(r11_q), .clk(CLK));  // open: clr
  Register #(.width(32)) u_r15 (.D(R15), .en(1'b1), .Q(r15_q), .clk(CLK));  // open: clr
  Multiplexer #(.select(4), .width(32), .enable("false")) multiplexer_1 (
    .in0(r0_q), .in1(r1_q), .in2(r2_q), .in3(r3_q), .in4(r4_q), .in5(r5_q), .in6(r6_q), .in7(r7_q),
    .in8(r8_q), .in9(r9_q), .in10(r10_q), .in11(r11_q), .in12(r12_q), .in13(r13_q), .in14(r14_q),
    .in15(r15_q), .out(RD1), .sel(A1));
  Multiplexer #(.select(4), .width(32), .enable("false")) multiplexer_2 (
    .in0(r0_q), .in1(r1_q), .in2(r2_q), .in3(r3_q), .in4(r4_q), .in5(r5_q), .in6(r6_q), .in7(r7_q),
    .in8(r8_q), .in9(r9_q), .in10(r10_q), .in11(r11_q), .in12(r12_q), .in13(r13_q), .in14(r14_q),
    .in15(r15_q), .out(RD2), .sel(A2));

  // Notes on the sheet:
  //   PC
endmodule

module ControlUnit (
  input  [3:0] Cond,
  input  [1:0] Opt,
  input  [5:0] Funct,
  input  [3:0] Rd,
  input  [3:0] Flags,
  output PCSrc,
  output MemtoReg,
  output MemWrite,
  output [1:0] ALUControl,
  output ALUSrc,
  output ImmSrc,
  output RegWrite,
  output [1:0] RegSrc
);
endmodule

module Extender (
  input  ImmSrc,
  input  [23:0] In,
  input  [31:0] Out
);
endmodule

module ALUw_Flags (
  input  [1:0] ALUControl,
  input  [31:0] B,
  input  [31:0] A,
  output [31:0] Result,
  output [3:0] ALUFlags
);

  wire adder_1_cout, not_2_out, not_3_out, Sum31, xor_1_out, xor_2_out, xor_3_out;
  wire [30:0] adder_1_out;
  wire [31:0] and_1_out, multiplexer_1_out, not_1_out, or_1_out;

  Multiplexer #(.width(32), .enable("false")) multiplexer_1 (
    .in0(B), .in1(not_1_out), .out(multiplexer_1_out), .sel(ALUControl[0]));
  assign not_1_out = ~B;  // NOT_Gate not_1, 32 bits wide
  not not_2 (not_2_out, ALUControl[1]);
  xor xor_1 (xor_1_out, B[31], A[31]);
  xor xor_2 (xor_2_out, xor_1_out, ALUControl[0]);
  xor xor_3 (xor_3_out, A[31], Sum31);
  not not_3 (not_3_out, xor_2_out);
  Adder #(.width(32)) adder_1 (
    .a(multiplexer_1_out), .b(A), .out({Sum31, adder_1_out}), .cin(ALUControl[0]), .cout(adder_1_cout));
  assign and_1_out = B & A;  // AND_Gate and_1, 32 bits wide
  assign or_1_out = B | A;  // OR_Gate or_1, 32 bits wide
  and and_2 (ALUFlags[1], adder_1_cout, not_2_out);
  and and_3 (ALUFlags[0], not_2_out, not_3_out, xor_3_out);
  Multiplexer #(.select(2), .width(32), .enable("false")) multiplexer_2 (
    .in0({Sum31, adder_1_out}), .in1({Sum31, adder_1_out}), .in2(and_1_out), .in3(or_1_out),
    .out({ALUFlags[3], Result[30:0]}), .sel(ALUControl));
  Comparator #(.width(32)) comparator_1 (
    .a({ALUFlags[3], Result[30:0]}), .b({32{1'b0}}), .eq(ALUFlags[2]));  // open: gt, lt

  assign Result[31] = ALUFlags[3];

  // Notes on the sheet:
  //   ALUControl1
  //   ALUControl0
  //   3 Input XNOR wegen Bug in XNOR
  //   Carry
  //   Overflow
  //   Zero
  //   Negative
endmodule
